# Fritzing sketch BBBW_Wiring (saved by Fritzing 0.9.3b)

parts:
  BeagleBone1 = BeagleBone Black
  S1 = Square Pushbutton
  LED1 = smd LED [color="Red (633nm)" package="1206 [SMD]"]
  R1 = Resistor [tolerance=±5% resistance=220 package="2512 [SMD]"]

nets:
  N1: BeagleBone1.no_name_yet#3, S1.leg1
  N2: BeagleBone1.no_name_yet#15, S1.leg0
  N3: BeagleBone1.no_name_yet#41, LED1.anode
  N4: BeagleBone1.no_name_yet#45, R1.Pin_1
  N5: LED1.cathode, R1.Pin_0

notes:
  P9_32 -- Potentiometer -- V+
  P9_34 -- Potentiometer -- Gnd
  P9_33 -- Potentiometer -- Sig
  P8_2 -- Servo -- Gnd
  P8_13 -- Servo -- Sig
  3.3 V
  Record button -- N.O.
  P9_15 -- Sig
  P9_41 -- LED

custom parts:
  BeagleBone Black: BeagleBone Black rev. A5B
